# Fritzing sketch wiring (saved by Fritzing 0.9.3b)
breadboards: 1

parts:
  Raspberry_Pi_1 = Raspberry Pi 3 [part_number=RPI-4]
  Pwr_BTN = Pushbutton [package="[THT]"]
  Pwr_LED = LED - 3mm [color="Red (633nm)" package="3 mm [THT]"]
  Q1 = NPN-Transistor [package="SOT-23 [SMD]"]
  Relay_attached_to_electric_door_latch = RELAY [package=relay-g5q]
  1 = Pushbutton [package="[SMD]"]
  2 = Pushbutton [package="[SMD]"]
  3 = Pushbutton [package="[SMD]"]
  6 = Pushbutton [package="[SMD]"]
  4 = Pushbutton [package="[SMD]"]
  5 = Pushbutton [package="[SMD]"]
  9 = Pushbutton [package="[SMD]"]
  7 = Pushbutton [package="[SMD]"]
  8 = Pushbutton [package="[SMD]"]
  0 = Pushbutton [package="[SMD]"]
  * = Pushbutton [package="[SMD]"]
  # = Pushbutton [package="[SMD]"]

nets:
  N1: Raspberry_Pi_1.GPIO3, Pwr_BTN.Pin_3, Pwr_BTN.Pin_4
  N2: Raspberry_Pi_1.GIPO4, Pwr_LED.cathode
  N3: Raspberry_Pi_1.GIPO17, 1.Pin_1, 1.Pin_2, 2.Pin_1, 2.Pin_2, 3.Pin_1, 3.Pin_2
  N4: Raspberry_Pi_1.GIPO27, 6.Pin_1, 6.Pin_2, 4.Pin_1, 4.Pin_2, 5.Pin_1, 5.Pin_2
  N5: Raspberry_Pi_1.GIPO22, 9.Pin_1, 9.Pin_2, 7.Pin_1, 7.Pin_2, 8.Pin_1, 8.Pin_2
  N6: Raspberry_Pi_1.GIPO10, 0.Pin_1, 0.Pin_2, *.Pin_1, *.Pin_2, #.Pin_1, #.Pin_2
  N7: Raspberry_Pi_1.GIPO6, Relay_attached_to_electric_door_latch.COIL2
  N8: Raspberry_Pi_1.GIPO13, Relay_attached_to_electric_door_latch.COIL1
  N9: Raspberry_Pi_1.GIPO24, 3.Pin_3, 3.Pin_4, 6.Pin_3, 6.Pin_4, 9.Pin_3
  N10: Raspberry_Pi_1.GIPO23, 2.Pin_3, 2.Pin_4, 5.Pin_3, 5.Pin_4, 8.Pin_3, 8.Pin_4, 0.Pin_3
  N11: Raspberry_Pi_1.GIPO18, 1.Pin_3, 1.Pin_4, 4.Pin_3, 4.Pin_4, 7.Pin_3, 7.Pin_4, *.Pin_3, *.Pin_4
  N12: Raspberry_Pi_1.GIPO15, Q1.0
  N13: Raspberry_Pi_1.GND, Pwr_BTN.Pin_1, Pwr_BTN.Pin_2, Pwr_LED.anode, Q1.2

notes:
  I used a latching relay. If you are not then you need to edit the configs/relay.py file.
  Connected to 5v fan
  controlled eith code from
  https://github.com/avt613/RPi-fan
  This is the same as a 3*4 membrane keypad
  Pwr BTN was setup with code from
  https://github.com/Howchoo/pi-power-button
  Pwr LED was setup with code from
  https://github.com/avt613/RPi-PWR-LED
  Camera not shown here
